// Logisim project project1.circ as structural Verilog: 5 circuits, main circuit main
module main (
  input  [15:0] in_1,
  input  [7:0] in_2,
  input  in,
  input  clr,
  output [15:0] LCM,
  output [15:0] GCD
);

  wire clock_1_out, control_unit_1_counter_plus_plus, control_unit_1_counter_reset, control_unit_1_gcden,
       control_unit_1_lcmen, control_unit_1_mulen, control_unit_1_s1, control_unit_1_s2, control_unit_1_s3,
       control_unit_1_s4, control_unit_1_s5, control_unit_1_s6, control_unit_1_t1en, control_unit_1_t2en,
       control_unit_1_writeen, datapath_1_x1, datapath_1_x2, datapath_1_y1, datapath_1_y2, datapath_1_y3,
       datapath_1_z;

  Clock clock_1 (.out(clock_1_out));
  control_unit control_unit_1 (
    .y1(datapath_1_y1), .y2(datapath_1_y2), .y3(datapath_1_y3), .x1(datapath_1_x1), .x2(datapath_1_x2),
    .z(datapath_1_z), .LCMEN(control_unit_1_lcmen), .GCDEN(control_unit_1_gcden),
    .mulEN(control_unit_1_mulen), .s1(control_unit_1_s1), .s2(control_unit_1_s2), .t2EN(control_unit_1_t2en),
    .s3(control_unit_1_s3), .t1EN(control_unit_1_t1en), .s4(control_unit_1_s4), .s5(control_unit_1_s5),
    .s6(control_unit_1_s6), .writeEN(control_unit_1_writeen), .counter_reset(control_unit_1_counter_reset),
    .counter_plus_plus(control_unit_1_counter_plus_plus), .in(in), .clr(clr), .clk(clock_1_out));
  datapath datapath_1 (
    .number(in_1), .n(in_2), .conter_plus_plus(control_unit_1_counter_plus_plus),
    .conter_RESET(control_unit_1_counter_reset), .WRITE_EN(control_unit_1_writeen), .s6(control_unit_1_s6),
    .s5(control_unit_1_s5), .s4(control_unit_1_s4), .t1EN(control_unit_1_t1en), .s3(control_unit_1_s3),
    .t2EN(control_unit_1_t2en), .s2(control_unit_1_s2), .s1(control_unit_1_s1), .mulEN(control_unit_1_mulen),
    .GCDEN(control_unit_1_gcden), .LCMEN(control_unit_1_lcmen), .clk(clock_1_out), .clr(clr), .GCD(GCD),
    .LCM(LCM), .y1(datapath_1_y1), .y2(datapath_1_y2), .y3(datapath_1_y3), .x1(datapath_1_x1),
    .x2(datapath_1_x2), .z(datapath_1_z));
endmodule

module ram32 (
  input  [15:0] number,
  input  [4:0] WHERETOWRITE,
  input  in_3,
  input  [4:0] WHERETOREAD,
  input  clk,
  input  in_6,
  output [15:0] READNUMBER
);

  wire decoder_1_out0, decoder_1_out1, decoder_1_out2, decoder_1_out3, decoder_1_out4, decoder_1_out5,
       decoder_1_out6, decoder_1_out7, decoder_1_out8, decoder_1_out9, decoder_1_out10, decoder_1_out11,
       decoder_1_out12, decoder_1_out13, decoder_1_out14, decoder_1_out15, decoder_1_out16, decoder_1_out17,
       decoder_1_out18, decoder_1_out19, decoder_1_out20, decoder_1_out21, decoder_1_out22, decoder_1_out23,
       decoder_1_out24, decoder_1_out25, decoder_1_out26, decoder_1_out27, decoder_1_out28, decoder_1_out29,
       decoder_1_out30, decoder_1_out31;
  wire [15:0] register_1_q, register_2_q, register_3_q, register_4_q, register_5_q, register_6_q,
       register_7_q, register_8_q, register_9_q, register_10_q, register_11_q, register_12_q, register_13_q,
       register_14_q, register_15_q, register_16_q, register_17_q, register_18_q, register_19_q,
       register_20_q, register_21_q, register_22_q, register_23_q, register_24_q, register_25_q,
       register_26_q, register_27_q, register_28_q, register_29_q, register_30_q, register_31_q,
       register_32_q;

  Decoder #(.select(5), .disabled(0)) decoder_1 (
    .out0(decoder_1_out0), .out1(decoder_1_out1), .out2(decoder_1_out2), .out3(decoder_1_out3),
    .out4(decoder_1_out4), .out5(decoder_1_out5), .out6(decoder_1_out6), .out7(decoder_1_out7),
    .out8(decoder_1_out8), .out9(decoder_1_out9), .out10(decoder_1_out10), .out11(decoder_1_out11),
    .out12(decoder_1_out12), .out13(decoder_1_out13), .out14(decoder_1_out14), .out15(decoder_1_out15),
    .out16(decoder_1_out16), .out17(decoder_1_out17), .out18(decoder_1_out18), .out19(decoder_1_out19),
    .out20(decoder_1_out20), .out21(decoder_1_out21), .out22(decoder_1_out22), .out23(decoder_1_out23),
    .out24(decoder_1_out24), .out25(decoder_1_out25), .out26(decoder_1_out26), .out27(decoder_1_out27),
    .out28(decoder_1_out28), .out29(decoder_1_out29), .out30(decoder_1_out30), .out31(decoder_1_out31),
    .sel(WHERETOWRITE), .en(in_3));
  Register #(.width(16)) register_1 (.D(number), .en(decoder_1_out0), .Q(register_1_q), .clk(clk), .clr(in_6));
  Register #(.width(16)) register_2 (.D(number), .en(decoder_1_out1), .Q(register_2_q), .clk(clk), .clr(in_6));
  Register #(.width(16)) register_3 (.D(number), .en(decoder_1_out2), .Q(register_3_q), .clk(clk), .clr(in_6));
  Register #(.width(16)) register_4 (.D(number), .en(decoder_1_out3), .Q(register_4_q), .clk(clk), .clr(in_6));
  Register #(.width(16)) register_5 (.D(number), .en(decoder_1_out4), .Q(register_5_q), .clk(clk), .clr(in_6));
  Register #(.width(16)) register_6 (.D(number), .en(decoder_1_out5), .Q(register_6_q), .clk(clk), .clr(in_6));
  Register #(.width(16)) register_7 (.D(number), .en(decoder_1_out6), .Q(register_7_q), .clk(clk), .clr(in_6));
  Register #(.width(16)) register_8 (.D(number), .en(decoder_1_out7), .Q(register_8_q), .clk(clk), .clr(in_6));
  Register #(.width(16)) register_9 (.D(number), .en(decoder_1_out8), .Q(register_9_q), .clk(clk), .clr(in_6));
  Register #(.width(16)) register_10 (.D(number), .en(decoder_1_out9), .Q(register_10_q), .clk(clk), .clr(in_6));
  Register #(.width(16)) register_11 (.D(number), .en(decoder_1_out10), .Q(register_11_q), .clk(clk), .clr(in_6));
  Register #(.width(16)) register_12 (.D(number), .en(decoder_1_out11), .Q(register_12_q), .clk(clk), .clr(in_6));
  Register #(.width(16)) register_13 (.D(number), .en(decoder_1_out12), .Q(register_13_q), .clk(clk), .clr(in_6));
  Register #(.width(16)) register_14 (.D(number), .en(decoder_1_out13), .Q(register_14_q), .clk(clk), .clr(in_6));
  Register #(.width(16)) register_15 (.D(number), .en(decoder_1_out14), .Q(register_15_q), .clk(clk), .clr(in_6));
  Register #(.width(16)) register_16 (.D(number), .en(decoder_1_out15), .Q(register_16_q), .clk(clk), .clr(in_6));
  Register #(.width(16)) register_17 (.D(number), .en(decoder_1_out16), .Q(register_17_q), .clk(clk), .clr(in_6));
  Register #(.width(16)) register_18 (.D(number), .en(decoder_1_out17), .Q(register_18_q), .clk(clk), .clr(in_6));
  Register #(.width(16)) register_19 (.D(number), .en(decoder_1_out18), .Q(register_19_q), .clk(clk), .clr(in_6));
  Register #(.width(16)) register_20 (.D(number), .en(decoder_1_out19), .Q(register_20_q), .clk(clk), .clr(in_6));
  Register #(.width(16)) register_21 (.D(number), .en(decoder_1_out20), .Q(register_21_q), .clk(clk), .clr(in_6));
  Register #(.width(16)) register_22 (.D(number), .en(decoder_1_out21), .Q(register_22_q), .clk(clk), .clr(in_6));
  Register #(.width(16)) register_23 (.D(number), .en(decoder_1_out22), .Q(register_23_q), .clk(clk), .clr(in_6));
  Register #(.width(16)) register_24 (.D(number), .en(decoder_1_out23), .Q(register_24_q), .clk(clk), .clr(in_6));
  Register #(.width(16)) register_25 (.D(number), .en(decoder_1_out24), .Q(register_25_q), .clk(clk), .clr(in_6));
  Register #(.width(16)) register_26 (.D(number), .en(decoder_1_out25), .Q(register_26_q), .clk(clk), .clr(in_6));
  Register #(.width(16)) register_27 (.D(number), .en(decoder_1_out26), .Q(register_27_q), .clk(clk), .clr(in_6));
  Register #(.width(16)) register_28 (.D(number), .en(decoder_1_out27), .Q(register_28_q), .clk(clk), .clr(in_6));
  Register #(.width(16)) register_29 (.D(number), .en(decoder_1_out28), .Q(register_29_q), .clk(clk), .clr(in_6));
  Register #(.width(16)) register_30 (.D(number), .en(decoder_1_out29), .Q(register_30_q), .clk(clk), .clr(in_6));
  Register #(.width(16)) register_31 (.D(number), .en(decoder_1_out30), .Q(register_31_q), .clk(clk), .clr(in_6));
  Register #(.width(16)) register_32 (.D(number), .en(decoder_1_out31), .Q(register_32_q), .clk(clk), .clr(in_6));
  Multiplexer #(.select(5), .width(16)) multiplexer_1 (
    .in0(register_1_q), .in1(register_2_q), .in2(register_3_q), .in3(register_4_q), .in4(register_5_q),
    .in5(register_6_q), .in6(register_7_q), .in7(register_8_q), .in8(register_9_q), .in9(register_10_q),
    .in10(register_11_q), .in11(register_12_q), .in12(register_13_q), .in13(register_14_q),
    .in14(register_15_q), .in15(register_16_q), .in16(register_17_q), .in17(register_18_q),
    .in18(register_19_q), .in19(register_20_q), .in20(register_21_q), .in21(register_22_q),
    .in22(register_23_q), .in23(register_24_q), .in24(register_25_q), .in25(register_26_q),
    .in26(register_27_q), .in27(register_28_q), .in28(register_29_q), .in29(register_30_q),
    .in30(register_31_q), .in31(register_32_q), .out(READNUMBER), .sel(WHERETOREAD));  // open: en
endmodule

module ram256 (
  input  [15:0] in_1,
  input  [7:0] WHERETOWRITE,
  input  EN,
  input  clk,
  input  clr,
  input  [7:0] WHERETOREAD,
  output [15:0] READNUMBER
);

  wire decoder_1_out0, decoder_1_out1, decoder_1_out2, decoder_1_out3, decoder_1_out4, decoder_1_out5,
       decoder_1_out6, decoder_1_out7;
  wire [15:0] ram32_1_readnumber, ram32_2_readnumber, ram32_3_readnumber, ram32_4_readnumber,
       ram32_5_readnumber, ram32_6_readnumber, ram32_7_readnumber, ram32_8_readnumber;

  Decoder #(.select(3), .disabled(0)) decoder_1 (
    .out0(decoder_1_out0), .out1(decoder_1_out1), .out2(decoder_1_out2), .out3(decoder_1_out3),
    .out4(decoder_1_out4), .out5(decoder_1_out5), .out6(decoder_1_out6), .out7(decoder_1_out7),
    .sel(WHERETOWRITE[7:5]), .en(EN));
  ram32 ram32_1 (
    .number(in_1), .WHERETOWRITE(WHERETOWRITE[4:0]), .in_3(decoder_1_out0), .clk(clk), .in_6(clr),
    .WHERETOREAD(WHERETOREAD[4:0]), .READNUMBER(ram32_1_readnumber));
  ram32 ram32_2 (
    .number(in_1), .WHERETOWRITE(WHERETOWRITE[4:0]), .in_3(decoder_1_out1), .clk(clk), .in_6(clr),
    .WHERETOREAD(WHERETOREAD[4:0]), .READNUMBER(ram32_2_readnumber));
  ram32 ram32_3 (
    .number(in_1), .WHERETOWRITE(WHERETOWRITE[4:0]), .in_3(decoder_1_out2), .clk(clk), .in_6(clr),
    .WHERETOREAD(WHERETOREAD[4:0]), .READNUMBER(ram32_3_readnumber));
  ram32 ram32_4 (
    .number(in_1), .WHERETOWRITE(WHERETOWRITE[4:0]), .in_3(decoder_1_out3), .clk(clk), .in_6(clr),
    .WHERETOREAD(WHERETOREAD[4:0]), .READNUMBER(ram32_4_readnumber));
  ram32 ram32_5 (
    .number(in_1), .WHERETOWRITE(WHERETOWRITE[4:0]), .in_3(decoder_1_out4), .clk(clk), .in_6(clr),
    .WHERETOREAD(WHERETOREAD[4:0]), .READNUMBER(ram32_5_readnumber));
  ram32 ram32_6 (
    .number(in_1), .WHERETOWRITE(WHERETOWRITE[4:0]), .in_3(decoder_1_out5), .clk(clk), .in_6(clr),
    .WHERETOREAD(WHERETOREAD[4:0]), .READNUMBER(ram32_6_readnumber));
  ram32 ram32_7 (
    .number(in_1), .WHERETOWRITE(WHERETOWRITE[4:0]), .in_3(decoder_1_out6), .clk(clk), .in_6(clr),
    .WHERETOREAD(WHERETOREAD[4:0]), .READNUMBER(ram32_7_readnumber));
  ram32 ram32_8 (
    .number(in_1), .WHERETOWRITE(WHERETOWRITE[4:0]), .in_3(decoder_1_out7), .clk(clk),
    .WHERETOREAD(WHERETOREAD[4:0]), .READNUMBER(ram32_8_readnumber));  // open: in_6
  Multiplexer #(.select(3), .width(16)) multiplexer_1 (
    .in0(ram32_1_readnumber), .in1(ram32_2_readnumber), .in2(ram32_3_readnumber), .in3(ram32_4_readnumber),
    .in4(ram32_5_readnumber), .in5(ram32_6_readnumber), .in6(ram32_7_readnumber), .in7(ram32_8_readnumber),
    .out(READNUMBER), .sel(WHERETOREAD[7:5]));  // open: en
endmodule

// data path
module datapath (
  input  s6,
  input  s3,
  input  [15:0] number,
  input  s2,
  input  conter_RESET,
  input  WRITE_EN,
  input  t2EN,
  input  conter_plus_plus,
  input  s5,
  input  mulEN,
  input  s4,
  input  t1EN,
  input  [7:0] n,
  input  GCDEN,
  input  s1,
  input  LCMEN,
  input  clk,
  input  clr,
  output y1,
  output y2,
  output y3,
  output x1,
  output x2,
  output [15:0] GCD,
  output [15:0] LCM,
  output z
);

  wire comparator_1_eq, comparator_1_gt, comparator_3_eq, comparator_4_eq, undriven;
  wire [7:0] adder_1_out, counter_q;
  wire [15:0] divider_1_out, mul_q, multiplexer_1_out, multiplexer_2_out, multiplexer_3_out,
       multiplexer_4_out, multiplexer_5_out, multiplexer_6_out, multiplexer_7_out, multiplexer_8_out,
       multiplexer_9_out, multiplier_1_out, ram256_1_readnumber, subtractor_1_out, subtractor_2_out, temp1_q,
       temp2_q;

  Adder adder_1 (.a(counter_q), .b(8'h1), .out(adder_1_out));  // open: cin, cout
  Register counter (.D(adder_1_out), .Q(counter_q), .clk(conter_plus_plus), .clr(conter_RESET));  // open: en
  or or_1 (x1, comparator_1_gt, comparator_1_eq);
  Comparator #(.mode("unsigned")) comparator_1 (
    .a(counter_q), .b(n), .gt(comparator_1_gt), .eq(comparator_1_eq), .lt(x2));
  ram256 ram256_1 (
    .in_1(number), .WHERETOWRITE(counter_q), .EN(WRITE_EN), .clk(clk), .clr(clr), .WHERETOREAD(counter_q),
    .READNUMBER(ram256_1_readnumber));
  Subtractor #(.width(16)) subtractor_1 (.a(temp2_q), .b(temp1_q), .out(subtractor_1_out));  // open: bin, bout
  Subtractor #(.width(16)) subtractor_2 (.a(temp1_q), .b(temp2_q), .out(subtractor_2_out));  // open: bin, bout
  Multiplexer #(.width(16), .enable("false")) multiplexer_1 (
    .in0(ram256_1_readnumber), .in1(LCM), .out(multiplexer_1_out), .sel(s6));
  Multiplexer #(.width(16)) multiplexer_2 (
    .in0(multiplexer_1_out), .in1(subtractor_1_out), .out(multiplexer_2_out), .sel(s3), .en(undriven));
  Multiplexer #(.width(16)) multiplexer_3 (
    .in0(ram256_1_readnumber), .in1(GCD), .out(multiplexer_3_out), .sel(s5));  // open: en
  Multiplexer #(.width(16)) multiplexer_4 (
    .in0(multiplexer_3_out), .in1(subtractor_2_out), .out(multiplexer_4_out), .sel(s4));  // open: en
  Register #(.width(16)) temp2 (.D(multiplexer_2_out), .en(t2EN), .Q(temp2_q), .clk(clk), .clr(clr));
  Register #(.width(16)) temp1 (.D(multiplexer_4_out), .en(t1EN), .Q(temp1_q), .clk(clk), .clr(clr));
  Comparator #(.width(16), .mode("unsigned")) comparator_2 (.a(temp2_q), .b(temp1_q), .gt(y1), .eq(y2), .lt(y3));
  Multiplexer #(.width(16)) multiplexer_5 (
    .in0(temp2_q), .in1(ram256_1_readnumber), .out(multiplexer_5_out), .sel(s2));  // open: en
  Multiplexer #(.width(16)) multiplexer_6 (.in0(temp1_q), .in1(LCM), .out(multiplexer_6_out), .sel(s2));  // open: en
  Divider #(.width(16)) divider_1 (.a(mul_q), .b(temp1_q), .out(divider_1_out));  // open: upper, rem
  Multiplier #(.width(16)) multiplier_1 (
    .a(multiplexer_5_out), .b(multiplexer_6_out), .out(multiplier_1_out));  // open: cin, cout
  Multiplexer #(.width(16)) multiplexer_7 (
    .in0(divider_1_out), .in1(ram256_1_readnumber), .out(multiplexer_7_out), .sel(s1));  // open: en
  Multiplexer #(.width(16)) multiplexer_8 (
    .in0(temp1_q), .in1(ram256_1_readnumber), .out(multiplexer_8_out), .sel(comparator_3_eq));  // open: en
  Multiplexer #(.width(16)) multiplexer_9 (
    .in0(multiplexer_7_out), .in1(ram256_1_readnumber), .out(multiplexer_9_out), .sel(comparator_3_eq));  // open: en
  Comparator #(.mode("unsigned")) comparator_3 (.a(n), .b(8'h1), .eq(comparator_3_eq));  // open: gt, lt
  Comparator #(.mode("unsigned")) comparator_4 (.a(counter_q), .b({8{1'b0}}), .eq(comparator_4_eq));  // open: gt, lt
  Register #(.width(16)) mul (.D(multiplier_1_out), .en(mulEN), .Q(mul_q), .clk(clk), .clr(clr));
  and and_1 (z, comparator_3_eq, comparator_4_eq);
  Register #(.width(16)) u_GCD (.D(multiplexer_8_out), .en(GCDEN), .Q(GCD), .clk(clk), .clr(clr));
  Register #(.width(16)) u_LCM (.D(multiplexer_9_out), .en(LCMEN), .Q(LCM), .clk(clk), .clr(clr));
endmodule

module control_unit (
  input  clk,
  input  y1,
  input  y2,
  input  y3,
  input  in,
  input  x1,
  input  x2,
  input  z,
  input  clr,
  output LCMEN,
  output GCDEN,
  output mulEN,
  output s1,
  output s2,
  output t2EN,
  output s3,
  output t1EN,
  output s4,
  output s5,
  output s6,
  output writeEN,
  output counter_reset,
  output counter_plus_plus
);

  wire and_1_out, and_2_out, and_3_out, and_4_out, and_5_out, and_6_out, and_7_out, and_8_out, and_9_out,
       and_10_out, and_11_out, and_12_out, and_13_out, and_14_out, and_15_out, and_16_out, decoder_1_out0,
       decoder_1_out1, decoder_1_out2, decoder_1_out4, decoder_1_out5, decoder_1_out6, decoder_1_out7,
       decoder_1_out9, decoder_1_out10, decoder_1_out11, decoder_1_out12, decoder_1_out13, decoder_1_out14,
       decoder_1_out15, decoder_1_out16, decoder_1_out18, decoder_1_out19, decoder_1_out20, decoder_1_out21,
       decoder_1_out23, decoder_1_out24, decoder_1_out25, decoder_1_out26, decoder_1_out27, decoder_1_out28,
       decoder_1_out29, decoder_1_out30, decoder_1_out31, not_1_out, not_2_out, or_1_out, or_2_out, or_3_out,
       or_4_out, or_5_out, or_6_out, or_7_out, or_8_out, or_9_out;
  wire [4:0] d_ff_5_q;

  or or_1 (or_1_out, decoder_1_out1, and_7_out, decoder_1_out4, decoder_1_out5, and_8_out, decoder_1_out9, decoder_1_out10, and_9_out, s2, and_10_out, decoder_1_out19, decoder_1_out20, decoder_1_out21, s6, and_11_out, decoder_1_out24, decoder_1_out25);
  or or_2 (or_2_out, and_12_out, writeEN, decoder_1_out5, and_13_out, decoder_1_out11, decoder_1_out12, decoder_1_out13, decoder_1_out14, and_14_out, decoder_1_out21, s6, decoder_1_out24, decoder_1_out25);
  or or_3 (or_3_out, and_15_out, s1, decoder_1_out9, decoder_1_out10, decoder_1_out11, decoder_1_out12, decoder_1_out13, decoder_1_out14, decoder_1_out23);
  or or_4 (or_4_out, and_1_out, decoder_1_out2, and_2_out, s1, decoder_1_out10, and_3_out, and_4_out, and_5_out, s6, and_6_out, decoder_1_out24, decoder_1_out25);
  and and_1 (and_1_out, in, decoder_1_out0);
  and and_2 (and_2_out, decoder_1_out6, z);
  and and_3 (and_3_out, decoder_1_out12, or_5_out);
  or or_5 (or_5_out, y1, y2);
  and and_4 (and_4_out, decoder_1_out16, x2);
  and and_5 (and_5_out, decoder_1_out18, or_6_out);
  or or_6 (or_6_out, y1, y2);
  and and_6 (and_6_out, decoder_1_out23, y3);
  and and_7 (and_7_out, decoder_1_out2, x2);
  and and_8 (and_8_out, decoder_1_out6, z);
  and and_9 (and_9_out, decoder_1_out12, or_7_out);
  or or_7 (or_7_out, y2, y3);
  and and_10 (and_10_out, decoder_1_out18, y1);
  and and_11 (and_11_out, decoder_1_out23, y2);
  and and_12 (and_12_out, decoder_1_out2, x1);
  and and_13 (and_13_out, decoder_1_out6, z);
  and and_14 (and_14_out, decoder_1_out18, or_8_out);
  or or_8 (or_8_out, y2, y3);
  not not_1 (not_1_out, z);
  and and_15 (and_15_out, not_1_out, decoder_1_out6);
  and and_16 (and_16_out, d_ff_5_q[4], not_2_out);
  or or_9 (or_9_out, and_16_out, decoder_1_out15);
  not not_2 (not_2_out, x1);
  Decoder #(.select(5)) decoder_1 (
    .out0(decoder_1_out0), .out1(decoder_1_out1), .out2(decoder_1_out2), .out3(writeEN),
    .out4(decoder_1_out4), .out5(decoder_1_out5), .out6(decoder_1_out6), .out7(decoder_1_out7), .out8(s1),
    .out9(decoder_1_out9), .out10(decoder_1_out10), .out11(decoder_1_out11), .out12(decoder_1_out12),
    .out13(decoder_1_out13), .out14(decoder_1_out14), .out15(decoder_1_out15), .out16(decoder_1_out16),
    .out17(s2), .out18(decoder_1_out18), .out19(decoder_1_out19), .out20(decoder_1_out20),
    .out21(decoder_1_out21), .out22(s6), .out23(decoder_1_out23), .out24(decoder_1_out24),
    .out25(decoder_1_out25), .out26(decoder_1_out26), .out27(decoder_1_out27), .out28(decoder_1_out28),
    .out29(decoder_1_out29), .out30(decoder_1_out30), .out31(decoder_1_out31), .sel(d_ff_5_q), .en(1'b1));
  D_Flip_Flop d_ff_1 (.clk(clk), .D(or_9_out), .Q(d_ff_5_q[4]), .en(1'b1), .reset(clr));  // open: Qn, preset
  D_Flip_Flop d_ff_2 (.clk(clk), .D(or_3_out), .Q(d_ff_5_q[3]), .en(1'b1), .reset(clr));  // open: Qn, preset
  D_Flip_Flop d_ff_3 (.clk(clk), .D(or_2_out), .Q(d_ff_5_q[2]), .en(1'b1), .reset(clr));  // open: Qn, preset
  or or_10 (LCMEN, decoder_1_out7, s1, decoder_1_out15, decoder_1_out26);
  D_Flip_Flop d_ff_4 (.clk(clk), .D(or_1_out), .Q(d_ff_5_q[1]), .en(1'b1), .reset(clr));  // open: Qn, preset
  or or_11 (GCDEN, decoder_1_out7, decoder_1_out15, decoder_1_out21);
  or or_12 (mulEN, decoder_1_out11, s2);
  or or_13 (t2EN, decoder_1_out10, decoder_1_out13, s2, decoder_1_out19, s6, decoder_1_out24);
  D_Flip_Flop d_ff_5 (.clk(clk), .D(or_4_out), .Q(d_ff_5_q[0]), .en(1'b1), .reset(clr));  // open: Qn, preset
  or or_14 (s3, decoder_1_out13, decoder_1_out19, decoder_1_out24);
  or or_15 (t1EN, s1, decoder_1_out14, s2, decoder_1_out20, s6, decoder_1_out25);
  or or_16 (s4, decoder_1_out14, decoder_1_out20, decoder_1_out25);
  or or_17 (counter_reset, decoder_1_out1, decoder_1_out5);
  or or_18 (counter_plus_plus, decoder_1_out4, decoder_1_out9, decoder_1_out11, decoder_1_out26);

  assign s5 = s2;
endmodule
